# Fritzing sketch Sketch 2 (saved by Fritzing 0.9.2b)
circuit board: 6.88566cm x 5.36311cm

parts:
  U6 = 74HC4052 [package=dil16]
  R1 = TRIMPOT [package=trimpot_pth_s3_lock]
  R2 = TRIMPOT [package=trimpot_pth_s3_lock]
  R3 = TRIMPOT [package=trimpot_pth_s3_lock]
  R4 = TRIMPOT [package=trimpot_pth_s3_lock]
  Part1 = Arduino Uno (Rev3)

nets:
  GND: U6.INH, U6.VEE, U6.GND, R1.CCW, R2.CCW, R3.CCW, R4.CCW, Part1.GND
  N1: U6.B, Part1.D2
  N2: U6.A, Part1.D4
  N3: U6.X3, R4.WIPER
  N4: U6.X0, R1.WIPER
  N5: U6.X, Part1.A0
  N6: U6.X1, R2.WIPER
  N7: U6.X2, R3.WIPER
  VCC: U6.VCC, R1.CW, R2.CW, R3.CW, R4.CW, Part1.5V
