# Fritzing sketch Untitled Sketch 2 (saved by Fritzing 0.9.2b)
circuit board: 8.46667cm x 5.64444cm
breadboards: 1

parts:
  U1 = 555 Timer [package="SO8 [SMD]"]
  R1 = PHOTOCELL [package=photocell-kit]
  R2 = Resistor [tolerance=±5% resistance=1k package=THT]
  VCC1 = Battery
  C2 = Tantalum Capacitor [capacitance=10µF package="C 6032 [SMD, tantalum]"]
  C1 = Ceramic Capacitor [capacitance=100nF package="100 mil [THT, multilayer]"]
  J1 = Piezo Speaker

nets:
  GND: U1.Pin_1, U1.Pin_2, U1.Pin_4, U1.Pin_6, U1.Pin_7, U1.Pin_8, R1.P$1, R1.P$2, R2.Pin_0, R2.Pin_1, VCC1.-, VCC1.+, C1.0, C1.1, J1.pin2
  N1: U1.Pin_3, C2.-, C2.+, J1.pin1
