# Fritzing sketch floating ball (saved by Fritzing 0.9.2b)
circuit board: 4.51101cm x 2.02569cm
breadboards: 1

parts:
  Part1 = LightBlue Bean
  LED1 = RGB LED - (4 legs) [package="5 mm [THT]"]
  R2 = Resistor [tolerance=±5% resistance=220 package=THT]
  J2 = female pin header, 4 pins [form="♀ (female)"]
  R3 = Resistor [tolerance=±5% resistance=220 package=THT]
  R1 = Resistor [tolerance=±5% resistance=220 package=THT]
  VCC1 = Battery
  J1 = female pin header, 3 pins [form="♀ (female)"]

nets:
  N1: Part1.D5/SCK, R1.Pin_1
  N2: Part1.D4/MISO, R2.Pin_1
  N3: Part1.D3/MOSI, R3.Pin_1
  N4: Part1.D2, J1.pin3
  N5: Part1.D1, J2.pin3
  N6: Part1.D0, J2.pin2
  N7: Part1.GND, LED1.common_anode, J2.pin4, VCC1.-, J1.pin2
  N8: Part1.BAT, J2.pin1, VCC1.+, J1.pin1
  N9: LED1.red_cathode, R3.Pin_0
  N10: LED1.green_cathode, R2.Pin_0
  N11: LED1.blue_cathode, R1.Pin_0
