# Fritzing sketch mini (saved by Fritzing 0.9.2b)
circuit board: 3.96743cm x 3.66033cm
breadboards: 1

parts:
  J3 = female pin header, 4 pins [form="♀ (female)"]
  J4 = female pin header, 3 pins [form="♀ (female)"]
  Part1 = Arduino Pro Mini v13
  J5 = female pin header, 4 pins [form="♀ (female)"]
  R1 = Resistor [tolerance=±5% resistance=220 package=THT]
  R2 = Resistor [tolerance=±5% resistance=220 package=THT]
  R3 = Resistor [tolerance=±5% resistance=220 package=THT]

nets:
  N1: J3.pin1, J4.pin3, Part1.VCC
  N2: J3.pin2, Part1.D4
  N3: J3.pin3, Part1.D2
  N4: J3.pin4, J4.pin1, Part1.GND, J5.pin2
  N5: J4.pin2, Part1.D6_PWM
  N6: Part1.D13/SCK, R2.Pin_0
  N7: Part1.D11_PWM/MOSI, R3.Pin_0
  N8: Part1.D8, R1.Pin_0
  N9: J5.pin1, R1.Pin_1
  N10: J5.pin3, R2.Pin_1
  N11: J5.pin4, R3.Pin_1

notes:
  touch sensor

// code stored in the sketch: mini.ino

